// Logisim project CPU.circ as structural Verilog: 3 circuits, main circuit CPU
// REGS
module RegisterBank (
  input  [15:0] DATA_IN,
  input  CHIP_ENABLE,
  input  ZERO_ENABLE,
  input  [2:0] ADDR,
  input  READ_WRITE,
  output [15:0] DATA_OUT
);

  wire clock_1_out, decoder_1_out0, decoder_1_out1, decoder_1_out2, decoder_1_out3, decoder_1_out4,
       decoder_1_out5, decoder_1_out6, decoder_1_out7, not_1_out;
  wire [15:0] controlled_buffer_1_out, controlled_buffer_2_out, multiplexer_1_out, Reg0_q, Reg1_q, Reg2_q,
       Reg3_q, Reg4_q, Reg5_q, Reg6_q, Reg7_q;

  Pull_Resistor pull_resistor_1 (.node(READ_WRITE));
  Decoder #(.select(3), .disabled(0)) decoder_1 (
    .out0(decoder_1_out0), .out1(decoder_1_out1), .out2(decoder_1_out2), .out3(decoder_1_out3),
    .out4(decoder_1_out4), .out5(decoder_1_out5), .out6(decoder_1_out6), .out7(decoder_1_out7), .sel(ADDR),
    .en(READ_WRITE));
  Clock clock_1 (.out(clock_1_out));
  assign controlled_buffer_1_out = CHIP_ENABLE ? DATA_IN : 16'bz;  // Controlled_Buffer controlled_buffer_1
  not not_1 (not_1_out, READ_WRITE);
  assign controlled_buffer_2_out = READ_WRITE ? controlled_buffer_1_out : 16'bz;  // Controlled_Buffer controlled_buffer_2
  Register #(.width(16), .trigger("high")) Reg0 (
    .D(controlled_buffer_2_out), .en(decoder_1_out0), .Q(Reg0_q), .clk(clock_1_out), .clr(ZERO_ENABLE));
  Register #(.width(16), .trigger("high")) Reg1 (
    .D(controlled_buffer_2_out), .en(decoder_1_out1), .Q(Reg1_q), .clk(clock_1_out));  // open: clr
  Register #(.width(16), .trigger("high")) Reg2 (
    .D(controlled_buffer_2_out), .en(decoder_1_out2), .Q(Reg2_q), .clk(clock_1_out));  // open: clr
  Register #(.width(16), .trigger("high")) Reg3 (
    .D(controlled_buffer_2_out), .en(decoder_1_out3), .Q(Reg3_q), .clk(clock_1_out));  // open: clr
  Register #(.width(16), .trigger("high")) Reg4 (
    .D(controlled_buffer_2_out), .en(decoder_1_out4), .Q(Reg4_q), .clk(clock_1_out));  // open: clr
  Register #(.width(16), .trigger("high")) Reg5 (
    .D(controlled_buffer_2_out), .en(decoder_1_out5), .Q(Reg5_q), .clk(clock_1_out));  // open: clr
  Register #(.width(16), .trigger("high")) Reg6 (
    .D(controlled_buffer_2_out), .en(decoder_1_out6), .Q(Reg6_q), .clk(clock_1_out));  // open: clr
  Register #(.width(16), .trigger("high")) Reg7 (
    .D(controlled_buffer_2_out), .en(decoder_1_out7), .Q(Reg7_q), .clk(clock_1_out));  // open: clr
  Pull_Resistor pull_resistor_2 (.node(not_1_out));
  Multiplexer #(.select(3), .width(16)) multiplexer_1 (
    .in0(Reg0_q), .in1(Reg1_q), .in2(Reg2_q), .in3(Reg3_q), .in4(Reg4_q), .in5(Reg5_q), .in6(Reg6_q),
    .in7(Reg7_q), .out(multiplexer_1_out), .sel(ADDR), .en(not_1_out));
  assign DATA_OUT = CHIP_ENABLE ? multiplexer_1_out : 16'bz;  // Controlled_Buffer controlled_buffer_3

  // Notes on the sheet:
  //   DATA_IN: pull=down
  //   ADDR: pull=down
endmodule

module ALU (
  input  [2:0] OPCODE_IN,
  input  READ_WRITE,
  input  [15:0] DATA_IN,
  input  ADDR,
  input  CHIP_ENABLE,
  output [15:0] DATA_OUT,
  output REGA___REGB,
  output REGA___REGB_2,
  output REGA___REGB_3
);

  wire button_1_out, button_2_out, clock_1_out, decoder_1_out0, decoder_1_out1, not_1_out;
  wire [15:0] adder_1_out, controlled_buffer_1_out, controlled_buffer_2_out, multiplexer_1_out, nand_1_out,
       RegA_q, RegB_q;

  Button button_1 (.out(button_1_out));
  Decoder #(.disabled(0)) decoder_1 (.out0(decoder_1_out0), .out1(decoder_1_out1), .sel(ADDR), .en(READ_WRITE));
  Button button_2 (.out(button_2_out));
  assign controlled_buffer_1_out = CHIP_ENABLE ? DATA_IN : 16'bz;  // Controlled_Buffer controlled_buffer_1
  assign controlled_buffer_2_out = READ_WRITE ? controlled_buffer_1_out : 16'bz;  // Controlled_Buffer controlled_buffer_2
  Register #(.width(16), .trigger("high")) RegA (
    .D(controlled_buffer_2_out), .en(decoder_1_out0), .Q(RegA_q), .clk(clock_1_out), .clr(button_1_out));
  Clock clock_1 (.out(clock_1_out));
  Register #(.width(16), .trigger("high")) RegB (
    .D(controlled_buffer_2_out), .en(decoder_1_out1), .Q(RegB_q), .clk(clock_1_out), .clr(button_2_out));
  Adder #(.width(16)) adder_1 (.a(RegA_q), .b(RegB_q), .out(adder_1_out));  // open: cin, cout
  assign nand_1_out = ~(RegA_q & RegB_q);  // NAND_Gate nand_1, 16 bits wide
  Comparator #(.width(16)) comparator_1 (
    .a(RegA_q), .b(RegB_q), .gt(REGA___REGB), .eq(REGA___REGB_2), .lt(REGA___REGB_3));
  not not_1 (not_1_out, READ_WRITE);
  Multiplexer #(.select(3), .width(16)) multiplexer_1 (
    .in0(adder_1_out), .in1(adder_1_out), .in2(nand_1_out), .out(multiplexer_1_out), .sel(OPCODE_IN),
    .en(not_1_out));  // open: in3, in4, in5, in6, in7
  assign DATA_OUT = CHIP_ENABLE ? multiplexer_1_out : 16'bz;  // Controlled_Buffer controlled_buffer_3

  // Notes on the sheet:
  //   REGA___REGB_3: pull=down
  //   REGA___REGB_2: pull=down
  //   CHIP_ENABLE: pull=down
  //   DATA_IN: pull=down
  //   REGA___REGB: pull=down
endmodule

module CPU (
  input  [15:0] in_1,
  input  [15:0] in_2,
  output BUS_R_W,
  output [15:0] out_4,
  output [22:0] ADDRESS_BUS
);

  wire _CLK, A_B, A_B_t, A_B_t_t, ALU_ENABLE, ALU_R_S, ALU_R_W, and_3_out, and_4_out, BRANCH, button_1_out,
       CLK, controlled_buffer_6_out, ENA_R_0, ENA_R_1, ENA_R_A, ENA_R_B, ENA_R_C, IMM_ENABLE, MEM_ACC,
       MPG_RST, NEXT_INSTR, NOP, not_1_out, not_2_out, not_3_out, or_1_out, or_3_out, PGC_INC, PGC_L,
       PGC_OVF, pull_resistor_1_node, pull_resistor_10_node, REG_ENABLE, REG_R_W, SEL_RW_0, SEL_RW_1;
  wire [1:0] MPG_CTR;
  wire [2:0] REG_ADDR;
  wire [5:0] undriven;
  wire [6:0] bit_extender_3_out, IMM_7;
  wire [7:0] rom_2_data;
  wire [9:7] IMM_10;
  wire [15:0] bit_extender_1_out, controlled_buffer_18_out, DATA_BUS;
  wire [15:10] INSTRUCTION;
  wire [22:0] adder_1_out, bit_extender_2_out, controlled_buffer_19_out, PGC, PGC_INP;

  RegisterBank RB1 (
    .DATA_IN(DATA_BUS), .DATA_OUT(DATA_BUS), .READ_WRITE(REG_R_W), .ADDR(REG_ADDR), .CHIP_ENABLE(REG_ENABLE),
    .ZERO_ENABLE(1'b1));
  // Probe on INSTRUCTION[12:10]
  assign REG_ADDR = ENA_R_A ? INSTRUCTION[12:10] : 3'bz;  // Controlled_Buffer controlled_buffer_1
  // Probe on IMM_10
  or or_1 (or_1_out, ENA_R_B, MEM_ACC);
  assign REG_ADDR = or_1_out ? IMM_10 : 3'bz;  // Controlled_Buffer controlled_buffer_2
  // Probe on IMM_7[2:0]
  assign REG_ADDR = ENA_R_C ? IMM_7[2:0] : 3'bz;  // Controlled_Buffer controlled_buffer_3
  Counter #(.width(23), .max('h7fffff), .ongoal("load"), .trigger("falling")) counter_1 (
    .load(PGC_L), .D(PGC_INP), .count(PGC_INC), .Q(PGC), .carry(PGC_OVF), .clk(_CLK), .clr(button_1_out));
  Button button_1 (.out(button_1_out));
  // Probe on INSTRUCTION[15:13]
  // Probe on INSTRUCTION[12:10]
  // Probe on IMM_7
  // Probe on {IMM_10, IMM_7}
  ALU alu_1 (
    .DATA_IN(DATA_BUS), .DATA_OUT(DATA_BUS), .REGA___REGB(A_B), .REGA___REGB_2(A_B_t),
    .REGA___REGB_3(A_B_t_t), .ADDR(ALU_R_S), .READ_WRITE(ALU_R_W), .OPCODE_IN(INSTRUCTION[15:13]),
    .CHIP_ENABLE(ALU_ENABLE));
  assign DATA_BUS = not_1_out ? in_1 : 16'bz;  // Controlled_Buffer controlled_buffer_4
  not not_1 (not_1_out, BUS_R_W);
  // Probe on DATA_BUS
  assign out_4 = BUS_R_W ? DATA_BUS : 16'bz;  // Controlled_Buffer controlled_buffer_5
  // Probe on IMM_10
  // Probe on IMM_7[2:0]
  Decoder #(.select(2), .disabled(0), .enable("false")) decoder_1 (
    .out1(REG_R_W), .out2(ALU_R_W), .out3(BUS_R_W), .sel({SEL_RW_1, SEL_RW_0}));  // open: out0
  // Probe on ADDRESS_BUS
  Decoder #(.select(2), .disabled(0), .enable("false")) decoder_2 (
    .out1(ENA_R_A), .out2(ENA_R_B), .out3(ENA_R_C), .sel({ENA_R_1, ENA_R_0}));  // open: out0
  and and_1 (BRANCH, INSTRUCTION[15], INSTRUCTION[14]);
  // Probe on DATA_BUS
  ROM #(.addrWidth(23), .dataWidth(16)) rom_1 (.addr(ADDRESS_BUS), .data(DATA_BUS), .sel(PGC_INC));
  or or_2 (REG_ENABLE, ENA_R_0, ENA_R_1);
  and and_2 (MEM_ACC, INSTRUCTION[15], ~INSTRUCTION[14]);  // AND_Gate
  Button button_2 (.out(MPG_RST));
  // Probe on MPG_CTR
  Counter #(.width(2), .max('h3), .trigger("falling")) counter_2 (
    .Q(MPG_CTR), .clk(CLK), .clr(controlled_buffer_6_out));  // open: load, D, count, carry
  assign controlled_buffer_6_out = CLK ? MPG_RST : 1'bz;  // Controlled_Buffer controlled_buffer_6
  Pull_Resistor #(.pull(1)) pull_resistor_1 (.node(pull_resistor_1_node));
  or or_3 (or_3_out, INSTRUCTION[15], ~INSTRUCTION[14], ~INSTRUCTION[13]);  // OR_Gate
  not not_2 (not_2_out, or_3_out);
  and and_3 (and_3_out, IMM_ENABLE, not_2_out);
  assign DATA_BUS = and_3_out ? {IMM_10, IMM_7, undriven} : 16'bz;  // Controlled_Buffer controlled_buffer_7
  Controlled_Buffer #(.width(3)) controlled_buffer_8 (.in(IMM_10), .en(MEM_ACC));  // open: out
  // Probe on INSTRUCTION[15:13]
  ROM #(.addrWidth(5)) rom_2 (.addr({INSTRUCTION[15:13], MPG_CTR}), .data(rom_2_data), .sel(pull_resistor_1_node));
  and and_4 (and_4_out, IMM_ENABLE, or_3_out);
  assign bit_extender_1_out = {{9{1'b0}}, IMM_7};  // Bit_Extender bit_extender_1
  assign DATA_BUS = and_4_out ? bit_extender_1_out : 16'bz;  // Controlled_Buffer controlled_buffer_9
  nor nor_1 (NOP, IMM_7[0], IMM_7[1], IMM_7[2], IMM_7[3], IMM_7[4], IMM_7[5], IMM_7[6], IMM_10[7], IMM_10[8], IMM_10[9], INSTRUCTION[10], INSTRUCTION[11], INSTRUCTION[12], INSTRUCTION[13], INSTRUCTION[14], INSTRUCTION[15]);
  not not_3 (not_3_out, NOP);
  assign SEL_RW_0 = not_3_out ? rom_2_data[0] : 1'bz;  // Controlled_Buffer controlled_buffer_10
  Pull_Resistor pull_resistor_2 (.node(SEL_RW_0));
  assign SEL_RW_1 = not_3_out ? rom_2_data[1] : 1'bz;  // Controlled_Buffer controlled_buffer_11
  assign ENA_R_0 = not_3_out ? rom_2_data[2] : 1'bz;  // Controlled_Buffer controlled_buffer_12
  assign ENA_R_1 = not_3_out ? rom_2_data[3] : 1'bz;  // Controlled_Buffer controlled_buffer_13
  assign ALU_R_S = not_3_out ? rom_2_data[4] : 1'bz;  // Controlled_Buffer controlled_buffer_14
  assign ALU_ENABLE = not_3_out ? rom_2_data[5] : 1'bz;  // Controlled_Buffer controlled_buffer_15
  assign IMM_ENABLE = not_3_out ? rom_2_data[6] : 1'bz;  // Controlled_Buffer controlled_buffer_16
  assign NEXT_INSTR = not_3_out ? rom_2_data[7] : 1'bz;  // Controlled_Buffer controlled_buffer_17
  Pull_Resistor pull_resistor_3 (.node(SEL_RW_1));
  Pull_Resistor pull_resistor_4 (.node(ENA_R_0));
  Pull_Resistor pull_resistor_5 (.node(ENA_R_1));
  Pull_Resistor pull_resistor_6 (.node(ALU_R_S));
  Pull_Resistor pull_resistor_7 (.node(ALU_ENABLE));
  Pull_Resistor pull_resistor_8 (.node(IMM_ENABLE));
  Pull_Resistor pull_resistor_9 (.node(NEXT_INSTR));
  Register #(.width(16), .trigger("high")) register_1 (
    .D(in_2), .Q({INSTRUCTION, IMM_10, IMM_7}), .clk(CLK));  // open: en, clr
  // Probe on {INSTRUCTION, IMM_10, IMM_7}
  // Probe on PGC
  and and_5 (PGC_L, INSTRUCTION[15], INSTRUCTION[14], ~INSTRUCTION[13], A_B_t, MPG_CTR[1], ~MPG_CTR[0]);  // AND_Gate
  // Probe on DATA_BUS
  assign controlled_buffer_18_out = PGC_L ? DATA_BUS : 16'bz;  // Controlled_Buffer controlled_buffer_18
  assign controlled_buffer_19_out = PGC_L ? PGC : 23'bz;  // Controlled_Buffer controlled_buffer_19
  not not_4 (_CLK, CLK);
  Clock clock_1 (.out(CLK));
  assign bit_extender_2_out = {{16{bit_extender_3_out[6]}}, bit_extender_3_out};  // Bit_Extender bit_extender_2
  Bit_Extender #(.in_width(16), .out_width(7)) bit_extender_3 (.in(controlled_buffer_18_out), .out(bit_extender_3_out));
  // Probe on controlled_buffer_19_out
  Pull_Resistor #(.pull(1)) pull_resistor_10 (.node(pull_resistor_10_node));
  Adder #(.width(23)) adder_1 (
    .a(bit_extender_2_out), .b(controlled_buffer_19_out), .out(adder_1_out), .cin(pull_resistor_10_node));  // open: cout
  // Probe on adder_1_out

  // Other names for the same wires on the sheet: OPCODE[2:0] = INSTRUCTION[15:13]; IMM_10[6:0] = IMM_7;
  //   INSTRUCTION[9:0] = {IMM_10, IMM_7}; RegC[2:0] = IMM_7[2:0]; RegB[2:0] = IMM_10; RegA[2:0] = INSTRUCTION[12:10];
  //   PGC_W = PGC_L

  // Notes on the sheet:
  //   in_2: pull=down
  //   in_1: pull=down
  //   BUS_R_W: pull=down
  //   contents of rom_2 (hex, n*v repeats v):
  //   2a 3e 25 80 2a 72 25 80 2a 3e 25 80 45 80 0 0 7 80 0 0 5 80 0 0 26 3a 40 80 5 80
endmodule
